// Logisim project Half adder.circ as structural Verilog: 1 circuit, main circuit Half Adder
module Half_Adder (
  input  x,
  input  y,
  output sum,
  output carry
);

  xor xor_1 (sum, x, y);
  and and_1 (carry, x, y);
endmodule
