// Logisim project Ripple carry adder.circ as structural Verilog: 2 circuits, main circuit Full Adder
module Full_Adder (
  input  x,
  input  y,
  input  z,
  output sum,
  output carry
);

  wire and_1_out, and_2_out, xor_1_out;

  xor xor_1 (xor_1_out, x, y);
  and and_1 (and_1_out, x, y);
  xor xor_2 (sum, xor_1_out, z);
  and and_2 (and_2_out, xor_1_out, z);
  xor xor_3 (carry, and_2_out, and_1_out);
endmodule

module Ripple_Carry_Adder (
  input  [3:0] A,
  input  [3:0] B,
  output [3:0] sum,
  output overflow
);

  wire full_adder_1_carry, full_adder_2_carry, full_adder_3_carry;

  Full_Adder full_adder_1 (.x(1'b1), .y(A[0]), .z(B[0]), .sum(sum[0]), .carry(full_adder_1_carry));
  Full_Adder full_adder_2 (.x(full_adder_1_carry), .y(A[1]), .z(B[1]), .sum(sum[1]), .carry(full_adder_2_carry));
  Full_Adder full_adder_3 (.x(full_adder_2_carry), .y(A[2]), .z(B[2]), .sum(sum[2]), .carry(full_adder_3_carry));
  Full_Adder full_adder_4 (.x(full_adder_3_carry), .y(A[3]), .z(B[3]), .sum(sum[3]), .carry(overflow));
endmodule
